# Fritzing sketch schema (saved by Fritzing 0.9.3b)
breadboards: 2

parts:
  Componente1 = Arduino Mega 2560 (Rev3)
  LED1 = smd LED [color="Red (633nm)" package="0805 [SMD]"]
  LED2 = smd LED [color="Red (633nm)" package="0805 [SMD]"]
  LED3 = smd LED [color="Red (633nm)" package="0805 [SMD]"]
  LED4 = smd LED [color="Red (633nm)" package="0805 [SMD]"]
  LED5 = smd LED [color="Red (633nm)" package="0805 [SMD]"]
  R1 = Resistor [tolerance=±5% resistance=220 package="1206 [SMD]"]
  R2 = Resistor [tolerance=±5% resistance=220 package="1206 [SMD]"]
  R3 = Resistor [tolerance=±5% resistance=220 package="1206 [SMD]"]
  R4 = Resistor [tolerance=±5% resistance=220 package="1206 [SMD]"]
  R5 = Resistor [tolerance=±5% resistance=220 package="1206 [SMD]"]
  Matrix_keypad1 = KEYPAD 4x4
  LCD1 = LCD screen
  R6 = Trimmer Potentiometer [maximum_resistance=10kΩ package=THT]
  R7 = Resistor [tolerance=±5% resistance=220 package="1206 [SMD]"]
  R8 = Resistor [tolerance=±5% resistance=220 package="1206 [SMD]"]
  R9 = Resistor [tolerance=±5% resistance=220 package="1206 [SMD]"]
  R10 = Resistor [tolerance=±5% resistance=220 package="1206 [SMD]"]
  7_Segment_4_Digit_Display2 = 7-SEGMENT-4DIGIT common cathode [part_number=HS420561K-32 package=7-segment-4digit-cathode]

nets:
  N1: Componente1.D13_PWM, 7_Segment_4_Digit_Display2.pin_3
  N2: Componente1.D12_PWM, 7_Segment_4_Digit_Display2.pin_10
  N3: Componente1.D11_PWM, 7_Segment_4_Digit_Display2.pin_5
  N4: Componente1.D10_PWM, 7_Segment_4_Digit_Display2.pin_1
  N5: Componente1.D9_PWM, 7_Segment_4_Digit_Display2.pin_2
  N6: Componente1.D8_PWM, 7_Segment_4_Digit_Display2.pin_4
  5V: Componente1.5V, LCD1.VDD, LCD1.LED+, R6.leg1
  GND: Componente1.GND, LED1.cathode, LED2.cathode, LED3.cathode, LED4.cathode, LED5.cathode, LCD1.VSS, LCD1.R/W, LCD1.LED-, R6.leg2
  N7: Componente1.D2_PWM, R7.Pin_1
  N8: Componente1.D3_PWM, R8.Pin_1
  N9: Componente1.D4_PWM, R9.Pin_1
  N10: Componente1.D5_PWM, R10.Pin_1
  N11: Componente1.D6_PWM, 7_Segment_4_Digit_Display2.pin_11
  N12: Componente1.D7_PWM, 7_Segment_4_Digit_Display2.pin_7
  N13: Componente1.D22, LCD1.RS
  N14: Componente1.D23, LCD1.E
  N15: Componente1.D24, LCD1.DB4
  N16: Componente1.D25, LCD1.DB5
  N17: Componente1.D26, LCD1.DB6
  N18: Componente1.D27, LCD1.DB7
  N19: Componente1.D34, Matrix_keypad1.col1
  N20: Componente1.D35, Matrix_keypad1.col2
  N21: Componente1.D36, Matrix_keypad1.col3
  N22: Componente1.D37, Matrix_keypad1.col4
  N23: Componente1.D38, Matrix_keypad1.row1
  N24: Componente1.D39, Matrix_keypad1.row2
  N25: Componente1.D40, Matrix_keypad1.row3
  N26: Componente1.D41, Matrix_keypad1.row4
  N27: Componente1.D49, R1.Pin_1
  N28: Componente1.D50, R2.Pin_1
  N29: Componente1.D51, R3.Pin_1
  N30: Componente1.D52, R4.Pin_1
  N31: Componente1.D53, R5.Pin_1
  N32: LED1.anode, R1.Pin_0
  N33: LED2.anode, R2.Pin_0
  N34: LED3.anode, R3.Pin_0
  N35: LED4.anode, R4.Pin_0
  N36: LED5.anode, R5.Pin_0
  N37: LCD1.V0, R6.wiper
  N38: R7.Pin_0, 7_Segment_4_Digit_Display2.pin_12
  N39: R8.Pin_0, 7_Segment_4_Digit_Display2.pin_9
  N40: R9.Pin_0, 7_Segment_4_Digit_Display2.pin_8
  N41: R10.Pin_0, 7_Segment_4_Digit_Display2.pin_6

custom parts:
  KEYPAD 4x4: Matrix keypad 16 buttons, 4 rows x 4 columns
  7-SEGMENT-4DIGIT common cathode: A 7 Segment 4 Digit common cathode display, with decimal points

// code stored in the sketch: Arduino___adivina.ino
#include <LiquidCrystal.h>
#include <Keypad.h>

LiquidCrystal lcd(22, 23, 24, 25, 26, 27);

const byte ROWS = 4;
const byte COLS = 4;
//D: ENVIAR
char hexaKeys[ROWS][COLS] = {
  {
    '1', '2', '3', 'A'
  }
  ,
  {
    '4', '5', '6', 'B'
  }
  ,
  {
    '7', '8', '9', 'C'
  }
  ,
  {
    '*', '0', '#', 'D'
  }
};
byte colPins[COLS] = {
  38,39,40,41
};
byte rowPins[ROWS] = {
  34,35,36,37
};

Keypad customKeypad = Keypad( makeKeymap(hexaKeys), rowPins, colPins, ROWS, COLS);

String rndString;
const String nombreJuego = "Defuse the bomb";
String usuario = "";
String respuestaUsuario = "     ";
boolean finJuego = false;
unsigned int intervalo = 100;
unsigned int anteriorMilli=0;
int cuentaAtras = 600;
byte relojNum2 = 0;
byte relojNum3 = 6;
byte relojNum4 = 0;
byte relojNum5 = 0;

void setup() {
  Serial.begin(9600);
  lcd.begin(16, 2);
  //Leds
  pinMode(53,OUTPUT);
  pinMode(52,OUTPUT);
  pinMode(51,OUTPUT);
  pinMode(50,OUTPUT);
  pinMode(49,OUTPUT);
  //Numeros
  pinMode(2,OUTPUT);
  pinMode(3,OUTPUT);
  pinMode(4,OUTPUT);
  pinMode(5,OUTPUT);
  pinMode(6,OUTPUT);
  pinMode(7,OUTPUT);
  pinMode(8,OUTPUT);
  pinMode(9,OUTPUT);
  pinMode(10,OUTPUT);
  pinMode(11,OUTPUT);
  pinMode(12,OUTPUT);
  pinMode(13,OUTPUT);
  randomSeed(analogRead(A0));
  calcularRandom();
  lcd.print(nombreJuego);
}

void loop() {
  displayNumbers();
  boolean acierto = false;
  if (!finJuego){
    unsigned int actualMilli = millis();
    if((unsigned int)(actualMilli - anteriorMilli) >= intervalo){
      cuentaAtras-=1;
      anteriorMilli+=intervalo;
      modificarReloj();
      Serial.println(cuentaAtras);
      Serial.println(relojNum2);
      Serial.println(relojNum3);
      Serial.println(relojNum4);
      Serial.println(relojNum5);
    }
    char customKey = customKeypad.getKey();
    acierto = comprobar();
    if (customKey) {
      switch (customKey) {
      case 'C':
      case 'A':
      case 'B':
        break;
      case '#':
      case '*':
        respuestaUsuario = usuario;
        break;
      case 'D':
        lcd.clear();
        lcd.print(nombreJuego);
        usuario = usuario.substring(0, usuario.length() - 1);
        break;
      default:
        if (usuario.length() < 5) {
          usuario += customKey;
        }
        break;
      }
      lcd.clear();
      lcd.print(nombreJuego);
      lcd.setCursor(0, 1);
      lcd.print(usuario);
    }
    if(acierto == true){
      lcd.clear();
      lcd.print("BOMB DEFUSE");
      lcd.setCursor(0, 1);
      lcd.print(usuario);
      finJuego = true;
    } else if(cuentaAtras <= 0){
      lcd.clear();
      lcd.print("BOOOOOOOOOOOOOMB");
      lcd.setCursor(0, 1);
      lcd.print("YOU ARE DIE");
      finJuego = true;
    }
  }
}

void calcularRandom(){
  int rnd = random(0,99999);
  rndString = String(rnd);
  if(rndString.charAt(0) == '-'){
    rndString = rndString.substring(1,rndString.length());
  }
  if(rndString.length()<5){
    byte n = 5 - rndString.length();
    for(byte i=0;i<n;i++){
      rndString = "0" + rndString;
    }
  }
}

boolean comprobar(){
  boolean acertado = false;
  byte aciertos = 0;
  if(respuestaUsuario.charAt(0) == rndString.charAt(0)){
    digitalWrite(49, HIGH);
    aciertos++;
  }
  if(respuestaUsuario.charAt(1) == rndString.charAt(1)){
    digitalWrite(50, HIGH);
    aciertos++;
  }
  if(respuestaUsuario.charAt(2) == rndString.charAt(2)){
    digitalWrite(51, HIGH);
    aciertos++;
  }
  if(respuestaUsuario.charAt(3) == rndString.charAt(3)){
    digitalWrite(52, HIGH);
    aciertos++;
  }
  if(respuestaUsuario.charAt(4) == rndString.charAt(4)){
    digitalWrite(53, HIGH);
    aciertos++;
  }
  if(aciertos >= 5){
    acertado = true;
  }
  return acertado;
}

void modificarReloj(){
  relojNum5--;
  if(relojNum5 > 10){
    relojNum5 = 9;
    relojNum4--;
  } else if(relojNum4 > 10){
    relojNum4 = 9;
    relojNum3--;
  } else if(relojNum3 > 10){
    relojNum3 = 5;
  } 
}

void displayNumbers(){
  displayOneNumber(2,relojNum2);
  displayOneNumber(3,relojNum3);
  displayOneNumber(4,relojNum4);
  displayOneNumber(5,relojNum5);
}

void displayOneNumber(byte pos, byte num){
  displayClear();
  switch(pos){
    case 2:
      digitalWrite(2, LOW);
      break;
    case 3:
      digitalWrite(3, LOW);
      break;
    case 4:
      digitalWrite(4, LOW);
      digitalWrite(13, HIGH);
      break;
    case 5:
      digitalWrite(5, LOW);
      break;
  }
  switch(num){
    case 0:
      digitalWrite(6, HIGH);
      digitalWrite(7, HIGH);
      digitalWrite(8, HIGH);
      digitalWrite(9, HIGH);
      digitalWrite(10, HIGH);
      digitalWrite(12, HIGH);
      break;
    case 1:
      digitalWrite(7, HIGH);
      digitalWrite(8, HIGH);
      break;
    case 2:
      digitalWrite(6, HIGH);
      digitalWrite(7, HIGH);
      digitalWrite(11, HIGH);
      digitalWrite(10, HIGH);
      digitalWrite(9, HIGH);
      break;
    case 3:
      digitalWrite(6, HIGH);
      digitalWrite(7, HIGH);
      digitalWrite(11, HIGH);
      digitalWrite(8, HIGH);
      digitalWrite(9, HIGH);
      break;
    case 4:
      digitalWrite(12, HIGH);
      digitalWrite(11, HIGH);
      digitalWrite(7, HIGH);
      digitalWrite(8, HIGH);
      break;
    case 5:
      digitalWrite(6, HIGH);
      digitalWrite(12, HIGH);
      digitalWrite(11, HIGH);
      digitalWrite(8, HIGH);
      digitalWrite(9, HIGH);
      break;
    case 6:
      digitalWrite(6, HIGH);
      digitalWrite(11, HIGH);
      digitalWrite(8, HIGH);
      digitalWrite(9, HIGH);
      digitalWrite(10, HIGH);
      digitalWrite(12, HIGH);
      break;
    case 7:
      digitalWrite(6, HIGH);
      digitalWrite(7, HIGH);
      digitalWrite(8, HIGH);
      break;
    case 8:
      digitalWrite(6, HIGH);
      digitalWrite(7, HIGH);
      digitalWrite(8, HIGH);
      digitalWrite(9, HIGH);
      digitalWrite(10, HIGH);
      digitalWrite(11, HIGH);
      digitalWrite(12, HIGH);
      break;
    case 9:
      digitalWrite(6, HIGH);
      digitalWrite(7, HIGH);
      digitalWrite(8, HIGH);
      digitalWrite(9, HIGH);
      digitalWrite(11, HIGH);
      digitalWrite(12, HIGH);
      break;
  }
}

void displayClear(){
  digitalWrite(2, HIGH);
  digitalWrite(3, HIGH);
  digitalWrite(4, HIGH);
  digitalWrite(5, HIGH);
  digitalWrite(6, LOW);
  digitalWrite(7, LOW);
  digitalWrite(8, LOW);
  digitalWrite(9, LOW);
  digitalWrite(10, LOW);
  digitalWrite(11, LOW);
  digitalWrite(12, LOW);
  digitalWrite(13, LOW);
}
